// Digital circuit state_char.dig as structural Verilog
module state_char (
  input  [7:0] D,
  output next,
  output done,
  output send,
  output fill
);

  wire not_1_out, not_2_out;

  not not_1 (not_1_out, D[0]);
  and and_1 (next, not_1_out, D[3], D[1]);
  and and_2 (done, not_1_out, D[3], D[2]);
  and and_3 (send, not_1_out, D[3], D[4]);
  not not_2 (not_2_out, D[3]);
  and and_4 (fill, not_1_out, not_2_out);
endmodule
